// Logisim project DSD_LAB10.circ as structural Verilog: 1 circuit, main circuit main
module main (
  input  in_1,
  input  s0,
  input  s1,
  input  sRight,
  input  sLeft,
  input  I1,
  input  I2,
  input  I0,
  input  I3,
  output out_10,
  output out_11,
  output out_12,
  output out_13
);

  wire clock_1_out, multiplexer_1_out, multiplexer_2_out, multiplexer_3_out, multiplexer_4_out;

  Clock clock_1 (.out(clock_1_out));
  D_Flip_Flop d_ff_1 (.D(multiplexer_1_out), .clk(clock_1_out), .Q(out_10), .preset(in_1), .reset(in_1));  // open: Qn
  Multiplexer #(.select(2)) multiplexer_1 (
    .in0(out_10), .in1(sLeft), .in2(out_11), .in3(I0), .out(multiplexer_1_out), .sel({s1, s0}));
  D_Flip_Flop d_ff_2 (.D(multiplexer_2_out), .clk(clock_1_out), .Q(out_11), .preset(in_1), .reset(in_1));  // open: Qn
  Multiplexer #(.select(2)) multiplexer_2 (
    .in0(out_11), .in1(out_10), .in2(out_12), .in3(I1), .out(multiplexer_2_out), .sel({s1, s0}));
  D_Flip_Flop d_ff_3 (.D(multiplexer_3_out), .clk(clock_1_out), .Q(out_12), .preset(in_1), .reset(in_1));  // open: Qn
  Multiplexer #(.select(2)) multiplexer_3 (
    .in0(out_12), .in1(out_11), .in2(out_13), .in3(I2), .out(multiplexer_3_out), .sel({s1, s0}));
  D_Flip_Flop d_ff_4 (.D(multiplexer_4_out), .clk(clock_1_out), .Q(out_13), .preset(in_1), .reset(in_1));  // open: Qn
  Multiplexer #(.select(2)) multiplexer_4 (
    .in0(out_13), .in1(out_12), .in2(sRight), .in3(I3), .out(multiplexer_4_out), .sel({s1, s0}));
endmodule
