// Logisim project lookahead.circ as structural Verilog: 1 circuit, main circuit main
module main (
  input  [3:0] in_1,
  input  [3:0] in_2,
  input  c0,
  output S0,
  output P0,
  output c1,
  output G0,
  output S1,
  output P1,
  output c2,
  output G1,
  output S2,
  output P2,
  output c3,
  output G2,
  output S3,
  output P3,
  output c4,
  output G3
);

  wire and_5_out, and_6_out, and_7_out, and_8_out;

  xor xor_1 (P0, in_1[0], in_2[0]);
  and and_1 (G0, in_2[0], in_1[0]);
  xor xor_2 (P1, in_1[1], in_2[1]);
  and and_2 (G1, in_2[1], in_1[1]);
  xor xor_3 (P2, in_1[2], in_2[2]);
  and and_3 (G2, in_2[2], in_1[2]);
  xor xor_4 (P3, in_1[3], in_2[3]);
  and and_4 (G3, in_2[3], in_1[3]);
  xor xor_5 (S0, P0, c0);
  and and_5 (and_5_out, P0, c0);
  xor xor_6 (S1, P1, c1);
  and and_6 (and_6_out, P1, c1);
  and and_7 (and_7_out, P2, c2);
  and and_8 (and_8_out, P3, c3);
  xor xor_7 (S2, P2, c2);
  xor xor_8 (S3, P3, c3);
  or or_1 (c1, and_5_out, G0);
  or or_2 (c2, and_6_out, G1);
  or or_3 (c3, and_7_out, G2);
  or or_4 (c4, and_8_out, G3);
endmodule
